// Digital circuit control_bomba.dig as structural Verilog
module control_bomba (
  input  tanqueH,
  input  tanqueL,
  input  cisternaOK,
  input  cisternaL,
  output bomba
);

  wire and_1_out, rs_ff_as_1_q;

  RS_FF_AS rs_ff_as_1 (.S(tanqueH), .R(~tanqueL), .Q(rs_ff_as_1_q));  // open: nQ
  and and_1 (and_1_out, cisternaOK, cisternaL, ~tanqueH);  // And
  and and_2 (bomba, and_1_out, ~rs_ff_as_1_q);  // And
endmodule
